// Logisim project s-mips.circ as structural Verilog: 20 circuits, main circuit S-MIPS Board
module S_MIPS_Board (
  input  DESHABILITAR_DISPATCHER,
  output halt
);

  wire button_1_out, CLK, CS, d_ff_1_q, LCLR, LoadRAM, LoadRAMOn, LW, R_R_W, R_W, ram_dispatcher_1_finished,
       RCS, Reset_out, RST, TTY_EN;
  wire [2:0] KDB;
  wire [3:0] LMask, Mask, ram_1_read_time, ram_1_write_time, RMask;
  wire [6:0] KDB_DATA, TTY_DATA;
  wire [15:0] Addr, LAddr, RAddr;
  wire [31:0] I0, I1, I2, I3, LData, ram_1_data_out_0, ram_1_data_out_1, ram_1_data_out_2, ram_1_data_out_3,
       RI0, RI1, RI2, RI3;

  TTY #(.rows(25), .cols(80)) tty_1 (.data(TTY_DATA), .clk(CLK), .we(TTY_EN), .clr(RST));
  // Probe on TTY_DATA
  not not_1 (LoadRAMOn, ram_dispatcher_1_finished);
  RAM_Dispatcher ram_dispatcher_1 (
    .WriteTime(ram_1_write_time), .Clock(CLK), .Data(LData), .Address(LAddr), .Mask(LMask),
    .Finished(ram_dispatcher_1_finished), .Write(LW), .CLR(LCLR));
  Keyboard #(.buflen(64)) keyboard_1 (.clk(CLK), .re(KDB[0]), .avail(KDB[2]), .data(KDB_DATA));  // open: clr
  RAM ram_1 (
    .Address(RAddr), .Data_Out_0(ram_1_data_out_0), .Data_Out_1(ram_1_data_out_1),
    .Data_Out_2(ram_1_data_out_2), .Data_Out_3(ram_1_data_out_3), .Data_In_0(RI0), .Data_In_1(RI1),
    .Data_In_2(RI2), .Data_In_3(RI3), .Mask(RMask), .nRead_Write(R_R_W), .Chip_Select(RCS),
    .Read_Time(ram_1_read_time), .Reset(button_1_out), .Write_Time(ram_1_write_time));
  Button button_1 (.out(button_1_out));
  D_Flip_Flop d_ff_1 (.clk(CLK), .D(1'b1), .Q(d_ff_1_q), .reset(Reset_out));  // open: Qn, preset, en
  Button Reset (.out(Reset_out));
  S_MIPS s_mips_1 (
    .Kbd_Enable(KDB[0]), .Address(Addr), .Kbd_Clear(KDB[1]), .Kbd_Available(KDB[2]), .RAM_In_0(I0),
    .Kbd_ASCII_Data(KDB_DATA), .RAM_In_1(I1), .TTY_Enable(TTY_EN), .RAM_In_2(I2), .RAM_In_3(I3),
    .TTY_ASCII_Data(TTY_DATA), .Reset(RST), .RAM_Out_0(ram_1_data_out_0), .Clock(CLK),
    .RAM_Out_1(ram_1_data_out_1), .Stop(halt), .RAM_Out_2(ram_1_data_out_2), .RAM_Out_3(ram_1_data_out_3),
    .Mask(Mask), .Read_Time(ram_1_read_time), .Write_Time(ram_1_write_time), .nRead_Write(R_W),
    .Chip_Select(CS));
  D_Flip_Flop d_ff_2 (.clk(CLK), .D(d_ff_1_q), .Qn(LCLR), .reset(Reset_out));  // open: Q, preset, en
  or or_1 (RST, LCLR, LoadRAM);
  Clock clock_1 (.out(CLK));
  Multiplexer #(.width(32), .enable("false")) multiplexer_1 (.in0(I0), .in1(LData), .out(RI0), .sel(LoadRAM));
  Multiplexer #(.width(32), .enable("false")) multiplexer_2 (.in0(I1), .in1(LData), .out(RI1), .sel(LoadRAM));
  Multiplexer #(.width(32), .enable("false")) multiplexer_3 (.in0(I2), .in1(LData), .out(RI2), .sel(LoadRAM));
  Multiplexer #(.width(32), .enable("false")) multiplexer_4 (.in0(I3), .in1(LData), .out(RI3), .sel(LoadRAM));
  and and_1 (LoadRAM, ~DESHABILITAR_DISPATCHER, LoadRAMOn);  // AND_Gate
  Multiplexer #(.width(16), .enable("false")) multiplexer_5 (.in0(Addr), .in1(LAddr), .out(RAddr), .sel(LoadRAM));
  Multiplexer #(.width(4), .enable("false")) multiplexer_6 (.in0(Mask), .in1(LMask), .out(RMask), .sel(LoadRAM));
  Multiplexer #(.enable("false")) multiplexer_7 (.in0(CS), .in1(LW), .out(RCS), .sel(LoadRAM));
  Multiplexer #(.enable("false")) multiplexer_8 (.in0(R_W), .in1(LW), .out(R_R_W), .sel(LoadRAM));

  // Notes on the sheet:
  //   NO MODIFICAR
  //   Keyboard
endmodule

module RAM (
  input  [15:0] Address,
  input  [31:0] Data_In_0,
  input  [31:0] Data_In_1,
  input  [31:0] Data_In_2,
  input  [31:0] Data_In_3,
  input  [3:0] Mask,
  input  nRead_Write,
  input  Chip_Select,
  input  Reset,
  output [31:0] Data_Out_0,
  output [31:0] Data_Out_1,
  output [31:0] Data_Out_2,
  output [31:0] Data_Out_3,
  output [3:0] Read_Time,
  output [3:0] Write_Time
);

  wire and_2_out, and_3_out, and_4_out, and_5_out, and_6_out, and_7_out, and_8_out, and_9_out, Changed, CLK,
       comparator_2_eq, comparator_3_eq, comparator_4_eq, comparator_5_eq, comparator_6_eq, Count,
       demultiplexer_3_out0, Idle, Idle_q, Load, Load0, Load1, nand_1_out, or_1_out, or_2_out, or_3_out,
       or_4_out, or_5_out, or_6_out, or_7_out, or_8_out, or_9_out, or_10_out, Proc_q, Update_Mem, Zero_Time;
  wire [3:0] counter_1_q, multiplexer_1_out, subtractor_1_out;
  wire [31:0] register_1_q, register_2_q, register_3_q, register_4_q, register_5_q;

  // Probe on 4'b0011
  // Probe on 4'b0010
  Multiplexer #(.width(4), .enable("false")) multiplexer_1 (
    .in0(4'b0011), .in1(4'b0010), .out(multiplexer_1_out), .sel(nRead_Write));
  or or_1 (or_1_out, Idle, Update_Mem);
  or or_2 (or_2_out, ~Chip_Select, Reset);  // OR_Gate
  Subtractor #(.width(4)) subtractor_1 (.a(multiplexer_1_out), .b(4'b0010), .out(subtractor_1_out));  // open: bin, bout
  D_Flip_Flop u_Idle (.clk(CLK), .D(or_1_out), .Q(Idle_q), .preset(or_2_out));  // open: Qn, en, reset
  Demultiplexer #(.enable("false")) demultiplexer_1 (.out0(Idle), .out1(Load0), .in(Idle_q), .sel(Changed));
  // Probe on counter_1_q
  Counter #(.width(4), .max('hf)) counter_1 (
    .load(Load), .D(subtractor_1_out), .count(Count), .Q(counter_1_q), .clk(CLK), .clr(or_3_out));  // open: carry
  or or_3 (or_3_out, ~Chip_Select, Reset);  // OR_Gate
  Comparator #(.width(4), .mode("unsigned")) comparator_1 (
    .a(4'b0000), .b(counter_1_q), .eq(Zero_Time));  // open: gt, lt
  or or_4 (or_4_out, Count, Load0, Load1);
  Register #(.width(32)) register_1 (.D(Data_In_0), .en(Chip_Select), .Q(register_1_q), .clk(CLK), .clr(or_5_out));
  or or_5 (or_5_out, ~Chip_Select, Reset);  // OR_Gate
  Register #(.width(32)) register_2 (.D(Data_In_1), .en(Chip_Select), .Q(register_2_q), .clk(CLK), .clr(or_6_out));
  or or_6 (or_6_out, ~Chip_Select, Reset);  // OR_Gate
  Register #(.width(32)) register_3 (.D(Data_In_2), .en(Chip_Select), .Q(register_3_q), .clk(CLK), .clr(or_7_out));
  or or_7 (or_7_out, ~Chip_Select, Reset);  // OR_Gate
  Register #(.width(32)) register_4 (.D(Data_In_3), .en(Chip_Select), .Q(register_4_q), .clk(CLK), .clr(or_8_out));
  or or_8 (or_8_out, ~Chip_Select, Reset);  // OR_Gate
  Register #(.width(32)) register_5 (
    .D({{11{1'b1}}, nRead_Write, Mask, Address}), .en(Chip_Select), .Q(register_5_q), .clk(CLK),
    .clr(or_9_out));
  or or_9 (or_9_out, ~Chip_Select, Reset);  // OR_Gate
  D_Flip_Flop Proc (.clk(CLK), .D(or_4_out), .Q(Proc_q), .reset(or_10_out));  // open: Qn, preset, en
  or or_10 (or_10_out, ~Chip_Select, Reset);  // OR_Gate
  Demultiplexer #(.enable("false")) demultiplexer_2 (
    .out0(Count), .out1(Update_Mem), .in(demultiplexer_3_out0), .sel(Zero_Time));
  Demultiplexer #(.enable("false")) demultiplexer_3 (
    .out0(demultiplexer_3_out0), .out1(Load1), .in(Proc_q), .sel(Changed));
  Clock clock_1 (.out(CLK));
  Comparator #(.width(32)) comparator_2 (.a(register_1_q), .b(Data_In_0), .eq(comparator_2_eq));  // open: gt, lt
  Comparator #(.width(32)) comparator_3 (.a(register_2_q), .b(Data_In_1), .eq(comparator_3_eq));  // open: gt, lt
  Comparator #(.width(32)) comparator_4 (.a(register_3_q), .b(Data_In_2), .eq(comparator_4_eq));  // open: gt, lt
  Comparator #(.width(32)) comparator_5 (.a(register_4_q), .b(Data_In_3), .eq(comparator_5_eq));  // open: gt, lt
  Comparator #(.width(32)) comparator_6 (
    .a(register_5_q), .b({{11{1'b1}}, nRead_Write, Mask, Address}), .eq(comparator_6_eq));  // open: gt, lt
  nand nand_1 (nand_1_out, comparator_6_eq, comparator_2_eq, comparator_3_eq, comparator_4_eq, comparator_5_eq);
  and and_1 (Changed, nand_1_out, Chip_Select);
  or or_11 (Load, Count, Load1, Load0);
  and and_2 (and_2_out, Mask[0], Update_Mem, nRead_Write);
  and and_3 (and_3_out, Mask[1], Update_Mem, nRead_Write);
  and and_4 (and_4_out, Mask[2], Update_Mem, nRead_Write);
  and and_5 (and_5_out, Mask[3], Update_Mem, nRead_Write);
  RAM_part #(.addrWidth(16), .dataWidth(32), .bus("separate")) ram_1 (
    .addr(Address), .din(Data_In_0), .data(Data_Out_0), .str(and_2_out), .sel(Chip_Select), .clk(CLK),
    .ld(and_6_out), .clr(Reset));
  and and_6 (and_6_out, ~nRead_Write, Idle);  // AND_Gate
  RAM_part #(.addrWidth(16), .dataWidth(32), .bus("separate")) ram_2 (
    .addr(Address), .din(Data_In_1), .data(Data_Out_1), .str(and_3_out), .sel(Chip_Select), .clk(CLK),
    .ld(and_7_out), .clr(Reset));
  and and_7 (and_7_out, ~nRead_Write, Idle);  // AND_Gate
  RAM_part #(.addrWidth(16), .dataWidth(32), .bus("separate")) ram_3 (
    .addr(Address), .din(Data_In_2), .data(Data_Out_2), .str(and_4_out), .sel(Chip_Select), .clk(CLK),
    .ld(and_8_out), .clr(Reset));
  and and_8 (and_8_out, ~nRead_Write, Idle);  // AND_Gate
  RAM_part #(.addrWidth(16), .dataWidth(32), .bus("separate")) ram_4 (
    .addr(Address), .din(Data_In_3), .data(Data_Out_3), .str(and_5_out), .sel(Chip_Select), .clk(CLK),
    .ld(and_9_out), .clr(Reset));
  and and_9 (and_9_out, ~nRead_Write, Idle);  // AND_Gate

  assign Read_Time = 4'b0011;
  assign Write_Time = 4'b0010;

  // Other names for the same wires on the sheet: M0 = Mask[0]; M1 = Mask[1]; M2 = Mask[2]; M3 = Mask[3];
  //   RW = nRead_Write; CLR = Reset; CS = Chip_Select; Load2 = Count

  // Notes on the sheet:
  //   NO MODIFICAR
  //   excepto quizás los valores RT y WT
  //   BANK0
  //   BANK1
  //   BANK2
  //   BANK3
endmodule

module RAM_Dispatcher (
  input  [3:0] WriteTime,
  input  Clock,
  input  CLR,
  output [31:0] Data,
  output [15:0] Address,
  output [3:0] Mask,
  output Finished,
  output Write
);

  wire demultiplexer_2_out1, demultiplexer_3_out1, End, IDLE_q, IncAddr, Load, or_1_out, or_2_out, While_q,
       WriteEnd;
  wire [3:0] counter_1_q;
  wire [31:0] CurrentAddress_q;

  Counter #(.width(32), .max('hffffffff)) CurrentAddress (
    .count(IncAddr), .Q({CurrentAddress_q[31:18], Address, CurrentAddress_q[1:0]}), .clk(Clock), .clr(CLR));  // open: load, D, carry
  or or_1 (or_1_out, IncAddr, demultiplexer_3_out1, Finished);
  D_Flip_Flop IDLE (.clk(Clock), .D(or_1_out), .Q(IDLE_q), .preset(CLR));  // open: Qn, en, reset
  Demultiplexer #(.enable("false")) demultiplexer_1 (.out0(Load), .out1(Finished), .in(IDLE_q), .sel(End));
  D_Flip_Flop While (.clk(Clock), .D(or_2_out), .Q(While_q), .reset(CLR));  // open: Qn, preset, en
  or or_2 (or_2_out, Write, Load);
  RAM_part #(.addrWidth(18), .dataWidth(32)) ram_1 (
    .addr({Address, CurrentAddress_q[1:0]}), .data(Data), .clk(Clock));  // open: sel, ld, clr
  Demultiplexer #(.enable("false")) demultiplexer_2 (
    .out0(Write), .out1(demultiplexer_2_out1), .in(While_q), .sel(WriteEnd));
  Decoder #(.select(2)) decoder_1 (
    .out0(Mask[0]), .out1(Mask[1]), .out2(Mask[2]), .out3(Mask[3]), .sel(CurrentAddress_q[1:0]));  // open: en
  Demultiplexer #(.enable("false")) demultiplexer_3 (
    .out0(IncAddr), .out1(demultiplexer_3_out1), .in(demultiplexer_2_out1), .sel(End));
  Counter #(.width(4), .max('hf)) counter_1 (
    .load(Load), .D(WriteTime), .count(Write), .Q(counter_1_q), .clk(Clock));  // open: carry, clr
  Comparator #(.width(32)) comparator_1 (.a(Data), .b({32{1'b1}}), .eq(End));  // open: gt, lt
  Comparator #(.width(4)) comparator_2 (.a(4'b0000), .b(counter_1_q), .eq(WriteEnd));  // open: gt, lt

  // Other names for the same wires on the sheet: CLK = Clock; Count = Write; WT[3:0] = WriteTime
endmodule

module S_MIPS (
  input  Kbd_Available,
  input  [6:0] Kbd_ASCII_Data,
  input  [31:0] RAM_Out_0,
  input  [31:0] RAM_Out_1,
  input  Reset,
  input  [31:0] RAM_Out_2,
  input  Clock,
  input  [31:0] RAM_Out_3,
  input  [3:0] Read_Time,
  input  [3:0] Write_Time,
  output Kbd_Enable,
  output [15:0] Address,
  output Kbd_Clear,
  output TTY_Enable,
  output [6:0] TTY_ASCII_Data,
  output Stop,
  output [31:0] RAM_In_0,
  output [31:0] RAM_In_1,
  output [31:0] RAM_In_2,
  output [31:0] RAM_In_3,
  output [3:0] Mask,
  output nRead_Write,
  output Chip_Select
);

  wire ALU_Inst, d_ff_2_q, en_GI, en_PC, en_RF, Get_Data, Get_Inst, half, Jump_Inst, Mem_Inst, or_1_out,
       or_2_out, R_Inst, Ready_Data, Ready_Inst, Ready_Write, Stack_Inst, START, tty_Inst, Write, Write_Inst;
  wire [31:0] ADDRESS_t, DATA_INST, data_path_1_out_21, multiplexer_1_out, multiplexer_2_out,
       multiplexer_3_out, multiplexer_4_out, ram_handler_1_out_16, ram_handler_1_out_17,
       ram_handler_1_out_18, ram_handler_1_out_19;

  Multiplexer #(.width(32)) multiplexer_1 (
    .in0(RAM_Out_0), .in1(RAM_In_0), .out(multiplexer_1_out), .sel(Write));  // open: en
  Multiplexer #(.width(32)) multiplexer_2 (
    .in0(RAM_Out_1), .in1(RAM_In_0), .out(multiplexer_2_out), .sel(Write));  // open: en
  Multiplexer #(.width(32)) multiplexer_3 (
    .in0(RAM_Out_2), .in1(RAM_In_0), .out(multiplexer_3_out), .sel(Write));  // open: en
  Multiplexer #(.width(32)) multiplexer_4 (
    .in0(RAM_Out_3), .in1(RAM_In_0), .out(multiplexer_4_out), .sel(Write));  // open: en
  or or_1 (or_1_out, Stack_Inst, Mem_Inst);
  D_Flip_Flop #(.trigger("falling")) d_ff_1 (.clk(Clock), .D(Reset), .Q(START));  // open: Qn, preset, en, reset
  Control_Unit control_unit_1 (
    .in_1(START), .in_2(Write_Inst), .in_3(Ready_Write), .in_4(Ready_Inst), .in_5(Ready_Data),
    .in_6(ALU_Inst), .in_7(R_Inst), .in_8(tty_Inst), .in_9(Jump_Inst), .in_10(or_1_out), .in_11(Clock),
    .in_12(Reset), .out_13(en_RF), .out_14(Get_Data), .out_15(en_PC), .out_16(Get_Inst), .out_17(en_GI),
    .out_18(TTY_Enable), .out_19(Write), .out_20(Kbd_Enable), .out_21(Stop));
  D_Flip_Flop #(.trigger("falling")) d_ff_2 (
    .clk(Clock), .D(Get_Inst), .Q(d_ff_2_q), .en(or_2_out));  // open: Qn, preset, reset
  or or_2 (or_2_out, Get_Inst, Ready_Inst);
  RAM_Handler ram_handler_1 (
    .in_1(Clock), .in_2(Reset), .in_3(multiplexer_1_out), .in_4(multiplexer_2_out), .in_5(multiplexer_3_out),
    .in_6(multiplexer_4_out), .in_7(Read_Time), .in_8(Write), .in_9(Write_Time), .out_14(Mask),
    .out_15(Address), .in_10(Get_Data), .in_11(Get_Inst), .in_12(en_GI), .in_13(ADDRESS_t),
    .out_16(ram_handler_1_out_16), .out_17(ram_handler_1_out_17), .out_18(ram_handler_1_out_18),
    .out_19(ram_handler_1_out_19), .out_20(nRead_Write), .out_21(Ready_Inst), .out_22(Ready_Data),
    .out_23(Chip_Select), .out_24(Ready_Write));
  Data_Path data_path_1 (
    .in_1(Clock), .in_4(Reset), .in_9(Kbd_ASCII_Data), .in_2(en_RF), .in_5(en_PC), .in_3(Kbd_Available),
    .in_6(d_ff_2_q), .in_7(en_GI), .out_12(half), .out_17(tty_Inst), .out_13(ALU_Inst), .out_18(Mem_Inst),
    .out_14(R_Inst), .out_19(Stack_Inst), .out_15(Jump_Inst), .out_20(Write_Inst), .in_10(DATA_INST),
    .out_16(ADDRESS_t), .out_11(TTY_ASCII_Data), .out_21(data_path_1_out_21), .in_8(1'b1));
  Multiplexer #(.select(2), .width(32)) multiplexer_5 (
    .in0(ram_handler_1_out_16), .in1(ram_handler_1_out_17), .in2(ram_handler_1_out_18),
    .in3(ram_handler_1_out_19), .out(DATA_INST), .sel(ADDRESS_t[3:2]));  // open: en
  Auxiliar_SwapOutRam auxiliar_swapoutram_1 (.in_1(data_path_1_out_21), .out_2(RAM_In_0));

  assign Kbd_Clear = Reset;
  assign RAM_In_1 = RAM_In_0;
  assign RAM_In_2 = RAM_In_0;
  assign RAM_In_3 = RAM_In_0;

  // Other names for the same wires on the sheet: CLK = Clock; CS = Chip_Select; KBD_AVAIL = Kbd_Available;
  //   CLR = Reset; KBD_CLR = Reset; KBD_DATA[6:0] = Kbd_ASCII_Data; RAM_A[15:0] = Address; R_Out[31:0] = RAM_In_0;
  //   RAM_INPUT_0[31:0] = RAM_In_0; RAM_INPUT_1[31:0] = RAM_In_0; RAM_INPUT_2[31:0] = RAM_In_0;
  //   RAM_INPUT_3[31:0] = RAM_In_0; RAM_MASK[3:0] = Mask; RAM_OUTPUT_0[31:0] = RAM_Out_0;
  //   RAM_OUTPUT_1[31:0] = RAM_Out_1; RAM_OUTPUT_2[31:0] = RAM_Out_2; RAM_OUTPUT_3[31:0] = RAM_Out_3;
  //   RW = nRead_Write; TTY_DATA[6:0] = TTY_ASCII_Data

  // Notes on the sheet:
  //   RAM ADDRESS
  //   DATA FROM RAM
  //   DATA TO RAM
  //   DATA WRITE MASK
  //   RAM TIMING
  //   RAM CONTROL
  //   KEYBOARD
  //   TTY
  //   SEQUENCING
endmodule

module ALU (
  input  [31:0] A,
  input  [31:0] B,
  input  [3:0] Operation,
  input  in_4,
  input  in_5,
  output Z,
  output N,
  output [31:0] RESULT_OPERATION,
  output [31:0] Lo,
  output [31:0] Lo_2
);

  wire and_1_out, and_2_out, and_4_out, and_5_out, comparator_1_lt, comparator_2_lt, or_1_out, or_3_out;
  wire [0:0] tunnel;
  wire [31:0] A_and_B, A_B, A_B_t, A_B_t_t, A_B_t_t_t, A_nor_B, A_or_B, A_xor_B, multiplexer_4_out,
       multiplexer_5_out, multiplexer_6_out, multiplexer_7_out, multiplexer_8_out, multiplexer_10_out,
       negator_1_out, negator_2_out, OVF, REM, uA, uB;

  // Probe on A
  Multiplexer #(.width(32)) multiplexer_1 (.in0(A), .in1(negator_1_out), .out(uA), .sel(A[31]));  // open: en
  Negator #(.width(32)) negator_1 (.in(A), .out(negator_1_out));
  Multiplexer #(.width(32)) multiplexer_2 (.in0(B), .in1(negator_2_out), .out(uB), .sel(B[31]));  // open: en
  Negator #(.width(32)) negator_2 (.in(B), .out(negator_2_out));
  Multiplexer #(.select(4), .width(32)) multiplexer_3 (
    .in0(A_B_t), .in1(A_B_t_t), .in4({{31{1'b0}}, tunnel[0]}), .in5(A_and_B), .in6(A_or_B), .in7(A_nor_B),
    .in8(A_xor_B), .out(RESULT_OPERATION), .sel(Operation));  // open: in2, in3, in9, in10, in11, in12, in13, in14, in15, en
  // Probe on B
  Multiplexer #(.width(32)) multiplexer_4 (.in0(uA), .in1(A), .out(multiplexer_4_out), .sel(in_4));  // open: en
  Multiplexer #(.width(32)) multiplexer_5 (.in0(uB), .in1(B), .out(multiplexer_5_out), .sel(in_4));  // open: en
  Multiplexer #(.width(32)) multiplexer_6 (.in0(uA), .in1(A), .out(multiplexer_6_out), .sel(in_4));  // open: en
  Multiplexer #(.width(32)) multiplexer_7 (.in0(uB), .in1(B), .out(multiplexer_7_out), .sel(in_4));  // open: en
  Adder #(.width(32)) adder_1 (.a(A), .b(B), .out(A_B_t));  // open: cin, cout
  Subtractor #(.width(32)) subtractor_1 (.a(A), .b(B), .out(A_B_t_t));  // open: bin, bout
  Divider #(.width(32)) divider_1 (
    .a(multiplexer_4_out), .b(multiplexer_5_out), .out(A_B_t_t_t), .rem(REM));  // open: upper
  Multiplier #(.width(32)) multiplier_1 (
    .a(multiplexer_6_out), .b(multiplexer_7_out), .out(A_B), .cout(OVF));  // open: cin
  Multiplexer #(.width(32)) multiplexer_8 (
    .in0(A_B_t_t_t), .in1(A_B), .out(multiplexer_8_out), .sel(and_1_out));  // open: en
  and and_1 (and_1_out, ~Operation[0], Operation[1], ~Operation[2], ~Operation[3]);  // AND_Gate
  or or_1 (or_1_out, and_1_out, and_2_out);
  and and_2 (and_2_out, Operation[0], Operation[1], ~Operation[2], ~Operation[3]);  // AND_Gate
  Comparator #(.width(32)) comparator_1 (.a(uA), .b(uB), .lt(comparator_1_lt));  // open: gt, eq
  Multiplexer multiplexer_9 (.in0(comparator_1_lt), .in1(comparator_2_lt), .out(tunnel[0]), .sel(in_4));  // open: en
  Comparator #(.width(32)) comparator_2 (.a(A), .b(B), .lt(comparator_2_lt));  // open: gt, eq
  assign A_and_B = A & B;  // AND_Gate and_3, 32 bits wide
  assign A_or_B = A | B;  // OR_Gate or_2, 32 bits wide
  assign A_xor_B = A ^ B;  // XOR_Gate xor_1, 32 bits wide
  assign A_nor_B = ~(A | B);  // NOR_Gate nor_1, 32 bits wide
  Register #(.width(32)) u_Lo (.D(multiplexer_8_out), .en(or_1_out), .Q(Lo_2), .clk(in_5));  // open: clr
  Multiplexer #(.width(32)) multiplexer_10 (
    .in0(REM), .in1(OVF), .out(multiplexer_10_out), .sel(and_4_out));  // open: en
  and and_4 (and_4_out, ~Operation[0], Operation[1], ~Operation[2], ~Operation[3]);  // AND_Gate
  or or_3 (or_3_out, and_4_out, and_5_out);
  and and_5 (and_5_out, Operation[0], Operation[1], ~Operation[2], ~Operation[3]);  // AND_Gate
  // Probe on RESULT_OPERATION
  // Probe on Lo
  // Probe on Lo_2
  Register #(.width(32)) Hi (.D(multiplexer_10_out), .en(or_3_out), .Q(Lo), .clk(in_5));  // open: clr
  Comparator #(.width(32)) comparator_3 (.a(RESULT_OPERATION), .b({32{1'b0}}), .eq(Z), .lt(N));  // open: gt

  // Other names for the same wires on the sheet: A_sign = A[31]; B_sign = B[31]; CLK = in_5; Hi[31:0] = Lo;
  //   Lo_t[31:0] = Lo_2; Op[3:0] = Operation; RESULT[31:0] = RESULT_OPERATION; sign = in_4
endmodule

module ALU_Encoder (
  input  in_1,
  input  in_2,
  input  in_3,
  input  in_4,
  input  in_5,
  input  in_6,
  input  in_7,
  input  in_8,
  input  in_9,
  input  in_10,
  input  in_11,
  input  in_12,
  input  in_13,
  input  in_14,
  input  in_15,
  input  in_16,
  input  in_17,
  input  in_18,
  output sign,
  output Immediate,
  output [3:0] Code_Operation
);

  wire and___andi, div___divu, mult___mulu, or___ori, slt___sltu, slti___sltiu;

  or or_1 (sign, in_6, in_4, in_8, in_10);
  or or_2 (Code_Operation[0], in_3, and___andi, in_16, div___divu);
  or or_3 (Code_Operation[1], mult___mulu, in_16, or___ori, div___divu);
  or or_4 (Code_Operation[2], slt___sltu, and___andi, in_16, or___ori, slti___sltiu);
  or or_5 (and___andi, in_12, in_13);
  or or_6 (div___divu, in_6, in_7);
  or or_7 (slti___sltiu, in_10, in_11);
  or or_8 (Immediate, in_10, in_13, in_2, in_18, in_15);
  or or_9 (Code_Operation[3], in_17, in_18);
  or or_10 (mult___mulu, in_4, in_5);
  or or_11 (slt___sltu, in_8, in_9);
  or or_12 (or___ori, in_14, in_15);

  // Other names for the same wires on the sheet: add = in_1; addi = in_2; and = in_12; andi = in_13;
  //   xor___xori = Code_Operation[3]; div = in_6; divu = in_7; mult = in_4; mulu = in_5; nor = in_16; or = in_14;
  //   ori = in_15; slt = in_8; slti = in_10; sltiu = in_11; sltu = in_9; sub = in_3; xor = in_17; xori = in_18
endmodule

module Branch_Control (
  input  in_1,
  input  in_2,
  input  in_3,
  input  in_4,
  input  in_5,
  input  in_6,
  input  in_7,
  input  [25:0] in_8,
  input  [31:0] in_9,
  input  [31:0] in_10,
  input  [31:0] in_11,
  input  [15:0] in_12,
  output [31:0] OUTPUT
);

  wire and_1_out, and_2_out, and_3_out, and_4_out, and_5_out, comparator_1_eq, or_2_out, Rs___0, Rs____0,
       Rs___Rt;
  wire [1:0] or_3_out;
  wire [13:0] bit_extender_1_out;
  wire [31:0] PC___4, PC___4___4_offset;

  Adder #(.width(32)) adder_1 (.a(in_11), .b(32'h4), .out(PC___4));  // open: cin, cout
  assign bit_extender_1_out = {{13{in_12[15]}}, in_12[15]};  // Bit_Extender bit_extender_1
  Comparator #(.width(32)) comparator_1 (.a(in_9), .b({32{1'b0}}), .eq(comparator_1_eq), .lt(Rs___0));  // open: gt
  Comparator #(.width(32)) comparator_2 (.a(in_9), .b(in_10), .eq(Rs___Rt));  // open: gt, lt
  or or_1 (Rs____0, comparator_1_eq, Rs___0);
  Adder #(.width(32)) adder_2 (
    .a(PC___4), .b({bit_extender_1_out, in_12, 2'b00}), .out(PC___4___4_offset));  // open: cin, cout
  and and_1 (and_1_out, in_1, Rs___Rt);
  and and_2 (and_2_out, ~Rs___Rt, in_2);  // AND_Gate
  and and_3 (and_3_out, in_5, Rs____0);
  and and_4 (and_4_out, ~Rs____0, in_6);  // AND_Gate
  and and_5 (and_5_out, in_3, Rs___0);
  or or_2 (or_2_out, and_1_out, and_2_out, and_3_out, and_4_out, and_5_out);
  or or_3 (or_3_out[0], or_2_out, in_4);
  or or_4 (or_3_out[1], in_4, in_7);
  Multiplexer #(.select(2), .width(32)) multiplexer_1 (
    .in0(PC___4), .in1(PC___4___4_offset), .in2({in_11[31:28], in_8, 2'b00}), .in3(in_9), .out(OUTPUT),
    .sel(or_3_out));  // open: en

  // Other names for the same wires on the sheet: offset[15:0] = in_12; beq = in_1; bgtz = in_6; blez = in_5;
  //   bltz = in_3; bne = in_2; j = in_7; jr = in_4; Destination[25:0] = in_8; jump[31:2] = {in_11[31:28], in_8};
  //   PC[31:0] = in_11; Rs[31:0] = in_9; Rt[31:0] = in_10
endmodule

module PC (
  input  [31:0] IPC,
  input  ENABLE,
  input  CLOCK,
  input  RESET,
  output [31:0] OPC
);

  Register #(.width(32)) PC (.D(IPC), .en(ENABLE), .Q(OPC), .clk(CLOCK), .clr(RESET));

  // Other names for the same wires on the sheet: EN = ENABLE; RST = RESET
endmodule

module Register_File (
  input  [31:0] in_1,
  input  [4:0] DA,
  input  [4:0] AA,
  input  [4:0] BA,
  input  CLOCK,
  input  RESET,
  input  READ_WRITE,
  input  PUSH,
  input  POP,
  input  IN_PC,
  output [31:0] SP,
  output [31:0] A,
  output [31:0] B
);

  wire en_R00, en_R01, en_R02, en_R03, en_R04, en_R05, en_R06, en_R07, en_R08, en_R09, en_R10, en_R11,
       en_R12, en_R13, en_R14, en_R15, en_R16, en_R17, en_R18, en_R19, en_R20, en_R21, en_R22, en_R23,
       en_R24, en_R25, en_R26, en_R27, en_R28, en_R29, en_R30, en_R31, In31, or_1_out, or_2_out;
  wire [31:0] adder_1_out, multiplexer_3_out, multiplexer_4_out, R00_out, R01_out, R02_out, R03_out, R04_out,
       R05_out, R06_out, R07_out, R08_out, R09_out, R10_out, R11_out, R12_out, R13_out, R14_out, R15_out,
       R16_out, R17_out, R18_out, R19_out, R20_out, R21_out, R22_out, R23_out, R24_out, R25_out, R26_out,
       R27_out, R28_out, R29_out, R30_out, SP_t, subtractor_1_out;

  Register #(.width(32)) R00 (.D({32{1'b0}}), .en(en_R00), .Q(R00_out), .clk(CLOCK), .clr(RESET));
  Register #(.width(32)) R04 (.D(in_1), .en(en_R04), .Q(R04_out), .clk(CLOCK), .clr(RESET));
  Register #(.width(32)) R08 (.D(in_1), .en(en_R08), .Q(R08_out), .clk(CLOCK), .clr(RESET));
  Register #(.width(32)) R12 (.D(in_1), .en(en_R12), .Q(R12_out), .clk(CLOCK), .clr(RESET));
  Register #(.width(32)) R16 (.D(in_1), .en(en_R16), .Q(R16_out), .clk(CLOCK), .clr(RESET));
  Register #(.width(32)) R20 (.D(in_1), .en(en_R20), .Q(R20_out), .clk(CLOCK), .clr(RESET));
  Register #(.width(32)) R24 (.D(in_1), .en(en_R24), .Q(R24_out), .clk(CLOCK), .clr(RESET));
  Register #(.width(32)) R28 (.D(in_1), .en(en_R28), .Q(R28_out), .clk(CLOCK), .clr(RESET));
  Multiplexer #(.select(5), .width(32)) multiplexer_1 (
    .in0(R00_out), .in1(R01_out), .in2(R02_out), .in3(R03_out), .in4(R04_out), .in5(R05_out), .in6(R06_out),
    .in7(R07_out), .in8(R08_out), .in9(R09_out), .in10(R10_out), .in11(R11_out), .in12(R12_out),
    .in13(R13_out), .in14(R14_out), .in15(R15_out), .in16(R16_out), .in17(R17_out), .in18(R18_out),
    .in19(R19_out), .in20(R20_out), .in21(R21_out), .in22(R22_out), .in23(R23_out), .in24(R24_out),
    .in25(R25_out), .in26(R26_out), .in27(R27_out), .in28(R28_out), .in29(R29_out), .in30(R30_out),
    .in31(SP), .out(A), .sel(AA));  // open: en
  Register #(.width(32)) R01 (.D(in_1), .en(en_R01), .Q(R01_out), .clk(CLOCK), .clr(RESET));
  Register #(.width(32)) R05 (.D(in_1), .en(en_R05), .Q(R05_out), .clk(CLOCK), .clr(RESET));
  Register #(.width(32)) R09 (.D(in_1), .en(en_R09), .Q(R09_out), .clk(CLOCK), .clr(RESET));
  Register #(.width(32)) R13 (.D(in_1), .en(en_R13), .Q(R13_out), .clk(CLOCK), .clr(RESET));
  Register #(.width(32)) R17 (.D(in_1), .en(en_R17), .Q(R17_out), .clk(CLOCK), .clr(RESET));
  Register #(.width(32)) R21 (.D(in_1), .en(en_R21), .Q(R21_out), .clk(CLOCK), .clr(RESET));
  Register #(.width(32)) R25 (.D(in_1), .en(en_R25), .Q(R25_out), .clk(CLOCK), .clr(RESET));
  Register #(.width(32)) R29 (.D(in_1), .en(en_R29), .Q(R29_out), .clk(CLOCK), .clr(RESET));
  Register #(.width(32)) R02 (.D(in_1), .en(en_R02), .Q(R02_out), .clk(CLOCK), .clr(RESET));
  Register #(.width(32)) R06 (.D(in_1), .en(en_R06), .Q(R06_out), .clk(CLOCK), .clr(RESET));
  Register #(.width(32)) R10 (.D(in_1), .en(en_R10), .Q(R10_out), .clk(CLOCK), .clr(RESET));
  Register #(.width(32)) R14 (.D(in_1), .en(en_R14), .Q(R14_out), .clk(CLOCK), .clr(RESET));
  Register #(.width(32)) R18 (.D(in_1), .en(en_R18), .Q(R18_out), .clk(CLOCK), .clr(RESET));
  Register #(.width(32)) R22 (.D(in_1), .en(en_R22), .Q(R22_out), .clk(CLOCK), .clr(RESET));
  Register #(.width(32)) R26 (.D(in_1), .en(en_R26), .Q(R26_out), .clk(CLOCK), .clr(RESET));
  Register #(.width(32)) R30 (.D(in_1), .en(en_R30), .Q(R30_out), .clk(CLOCK), .clr(RESET));
  Multiplexer #(.select(5), .width(32)) multiplexer_2 (
    .in0(R00_out), .in1(R01_out), .in2(R02_out), .in3(R03_out), .in4(R04_out), .in5(R05_out), .in6(R06_out),
    .in7(R07_out), .in8(R08_out), .in9(R09_out), .in10(R10_out), .in11(R11_out), .in12(R12_out),
    .in13(R13_out), .in14(R14_out), .in15(R15_out), .in16(R16_out), .in17(R17_out), .in18(R18_out),
    .in19(R19_out), .in20(R20_out), .in21(R21_out), .in22(R22_out), .in23(R23_out), .in24(R24_out),
    .in25(R25_out), .in26(R26_out), .in27(R27_out), .in28(R28_out), .in29(R29_out), .in30(R30_out),
    .in31(SP), .out(B), .sel(BA));  // open: en
  Register #(.width(32)) R03 (.D(in_1), .en(en_R03), .Q(R03_out), .clk(CLOCK), .clr(RESET));
  Register #(.width(32)) R07 (.D(in_1), .en(en_R07), .Q(R07_out), .clk(CLOCK), .clr(RESET));
  Register #(.width(32)) R11 (.D(in_1), .en(en_R11), .Q(R11_out), .clk(CLOCK), .clr(RESET));
  Register #(.width(32)) R15 (.D(in_1), .en(en_R15), .Q(R15_out), .clk(CLOCK), .clr(RESET));
  Register #(.width(32)) R19 (.D(in_1), .en(en_R19), .Q(R19_out), .clk(CLOCK), .clr(RESET));
  Register #(.width(32)) R23 (.D(in_1), .en(en_R23), .Q(R23_out), .clk(CLOCK), .clr(RESET));
  Register #(.width(32)) R27 (.D(in_1), .en(en_R27), .Q(R27_out), .clk(CLOCK), .clr(RESET));
  Demultiplexer #(.select(5)) demultiplexer_1 (
    .out0(en_R00), .out1(en_R01), .out2(en_R02), .out3(en_R03), .out4(en_R04), .out5(en_R05), .out6(en_R06),
    .out7(en_R07), .out8(en_R08), .out9(en_R09), .out10(en_R10), .out11(en_R11), .out12(en_R12),
    .out13(en_R13), .out14(en_R14), .out15(en_R15), .out16(en_R16), .out17(en_R17), .out18(en_R18),
    .out19(en_R19), .out20(en_R20), .out21(en_R21), .out22(en_R22), .out23(en_R23), .out24(en_R24),
    .out25(en_R25), .out26(en_R26), .out27(en_R27), .out28(en_R28), .out29(en_R29), .out30(en_R30),
    .out31(In31), .in(READ_WRITE), .sel(DA));  // open: en
  Adder #(.width(32)) adder_1 (.a(32'h4), .b(SP), .out(adder_1_out));  // open: cin, cout
  Subtractor #(.width(32)) subtractor_1 (.a(SP), .b(32'h4), .out(subtractor_1_out));  // open: bin, bout
  or or_1 (or_1_out, PUSH, POP);
  Multiplexer #(.width(32)) multiplexer_3 (.in0(SP_t), .in1(in_1), .out(multiplexer_3_out), .sel(In31));  // open: en
  Multiplexer #(.width(32)) multiplexer_4 (
    .in0(subtractor_1_out), .in1(adder_1_out), .out(multiplexer_4_out), .sel(POP));  // open: en
  Multiplexer #(.width(32)) multiplexer_5 (
    .in0(multiplexer_4_out), .in1({32{1'b1}}), .out(SP_t), .sel(RESET));  // open: en
  and and_1 (en_R31, or_1_out, IN_PC);
  Register #(.width(32)) R31 (.D(multiplexer_3_out), .en(or_2_out), .Q(SP), .clk(CLOCK));  // open: clr
  or or_2 (or_2_out, en_R31, In31, RESET);

  // Other names for the same wires on the sheet: CLK = CLOCK; Data[31:0] = in_1; en_PC = IN_PC; R31_out[31:0] = SP;
  //   R_W = READ_WRITE; RST = RESET
endmodule

module ID_Intruction_Decoder (
  input  [31:0] Instruction,
  input  in_2,
  output [5:0] out_3,
  output [5:0] out_4,
  output [4:0] out_5,
  output [4:0] out_6,
  output [4:0] out_7,
  output [15:0] out_8,
  output [25:0] out_9,
  output out_10,
  output out_11,
  output out_12,
  output out_13,
  output out_14,
  output out_15,
  output out_16,
  output out_17,
  output out_18,
  output out_19,
  output out_20,
  output out_21,
  output out_22,
  output out_23,
  output out_24,
  output out_25,
  output out_26,
  output out_27,
  output out_28,
  output out_29,
  output out_30,
  output out_31,
  output out_32,
  output out_33,
  output out_34,
  output out_35,
  output out_36,
  output out_37,
  output out_38,
  output out_39,
  output out_40,
  output out_41,
  output out_42,
  output out_43,
  output out_44,
  output out_45
);

  ID_Op_Code_R id_op_code_r_1 (
    .Function_Code(Instruction[5:0]), .in_3(in_2), .nop(out_10), .add(out_14), .sub(out_18), .mult(out_22),
    .div(out_27), .divu(out_15), .mulu(out_11), .stl(out_19), .stlu(out_23), .\and (out_31), .\or (out_28),
    .\nor (out_32), .\xor (out_34), .Operation_Code(Instruction[31:26]), .pop(out_33), .push(out_38),
    .jr(out_39), .mfhi(out_40), .mflo(out_41), .half(out_42), .tty(out_43), .rnd(out_44), .kbd(out_45));
  ID_Op_Code_I id_op_code_i_1 (
    .Function_Code(Instruction[31:26]), .in_2(in_2), .addi(out_12), .stli(out_16), .stliu(out_20),
    .andi(out_13), .ori(out_17), .xori(out_21), .lw(out_24), .sw(out_25), .beq(out_29), .bne(out_30),
    .blez(out_36), .bgtz(out_37), .bltz(out_35));
  ID_Op_Code_J id_op_code_j_1 (.Operation_Code(Instruction[31:26]), .in_2(in_2), .jump(out_26));

  assign out_3 = Instruction[31:26];
  assign out_4 = Instruction[5:0];
  assign out_5 = Instruction[15:11];
  assign out_6 = Instruction[20:16];
  assign out_7 = Instruction[25:21];
  assign out_8 = Instruction[15:0];
  assign out_9 = Instruction[25:0];

  // Other names for the same wires on the sheet: EN = in_2; Constant[15:0] = Instruction[15:0];
  //   Function_Code[5:0] = Instruction[5:0]; Jump_Dest[25:0] = Instruction[25:0]; No_Use[4:0] = Instruction[10:6];
  //   Rd[4:0] = Instruction[15:11]; Rt[4:0] = Instruction[20:16]; Rs[4:0] = Instruction[25:21];
  //   Operation_Code[5:0] = Instruction[31:26]
endmodule

module ID_Op_Code_R (
  input  [5:0] Operation_Code,
  input  [5:0] Function_Code,
  input  in_3,
  output nop,
  output add,
  output sub,
  output mult,
  output mulu,
  output div,
  output divu,
  output stl,
  output stlu,
  output \and ,
  output \or ,
  output \nor ,
  output \xor ,
  output jr,
  output push,
  output pop,
  output mfhi,
  output mflo,
  output tty,
  output half,
  output rnd,
  output kbd
);

  wire and_1_out, and_2_out, and_3_out, and_4_out, and_5_out, and_6_out, and_7_out, and_8_out, and_17_out,
       and_19_out, and_21_out, and_23_out, and_25_out, and_26_out, and_27_out, and_29_out, and_31_out,
       and_35_out, and_37_out, and_39_out, and_41_out, and_43_out, and_45_out, and_47_out,
       Neccesary_Condition, ONC;

  and and_1 (and_1_out, ~Function_Code[0], ~Function_Code[1], ~Function_Code[2], ~Function_Code[3], ~Function_Code[4], Function_Code[5], in_3);  // AND_Gate
  and and_2 (and_2_out, Function_Code[0], ~Function_Code[1], ~Function_Code[2], Function_Code[3], Function_Code[4], ~Function_Code[5], in_3);  // AND_Gate
  and and_3 (and_3_out, ~Function_Code[0], Function_Code[1], ~Function_Code[2], Function_Code[3], ~Function_Code[4], Function_Code[5], in_3);  // AND_Gate
  and and_4 (and_4_out, Function_Code[0], ~Function_Code[1], Function_Code[2], ~Function_Code[3], ~Function_Code[4], Function_Code[5], in_3);  // AND_Gate
  and and_5 (and_5_out, Function_Code[0], ~Function_Code[1], ~Function_Code[2], ~Function_Code[3], ~Function_Code[4], ~Function_Code[5], in_3);  // AND_Gate
  and and_6 (and_6_out, ~Operation_Code[0], ~Operation_Code[1], ~Operation_Code[2], Operation_Code[3], Operation_Code[4], Operation_Code[5], in_3);  // AND_Gate
  and and_7 (and_7_out, ~Function_Code[0], ~Function_Code[1], ~Function_Code[2], ~Function_Code[3], Function_Code[4], ~Function_Code[5], in_3);  // AND_Gate
  and and_8 (and_8_out, Function_Code[0], Function_Code[1], Function_Code[2], Function_Code[3], Function_Code[4], Function_Code[5], in_3);
  and and_9 (add, Neccesary_Condition, and_1_out);
  and and_10 (mulu, Neccesary_Condition, and_2_out);
  and and_11 (stl, Neccesary_Condition, and_3_out);
  and and_12 (\or , Neccesary_Condition, and_4_out);
  and and_13 (push, and_5_out, and_6_out);
  and and_14 (mfhi, Neccesary_Condition, and_7_out);
  and and_15 (half, ONC, and_8_out);
  and and_16 (Neccesary_Condition, ~Operation_Code[0], ~Operation_Code[1], ~Operation_Code[2], ~Operation_Code[3], ~Operation_Code[4], ~Operation_Code[5], in_3);  // AND_Gate
  and and_17 (and_17_out, ~Function_Code[0], ~Function_Code[1], ~Function_Code[2], ~Function_Code[3], ~Function_Code[4], ~Function_Code[5], in_3);  // AND_Gate
  and and_18 (sub, Neccesary_Condition, and_19_out);
  and and_19 (and_19_out, ~Function_Code[0], Function_Code[1], ~Function_Code[2], ~Function_Code[3], ~Function_Code[4], Function_Code[5], in_3);  // AND_Gate
  and and_20 (div, Neccesary_Condition, and_21_out);
  and and_21 (and_21_out, ~Function_Code[0], Function_Code[1], ~Function_Code[2], Function_Code[3], Function_Code[4], ~Function_Code[5], in_3);  // AND_Gate
  and and_22 (stlu, Neccesary_Condition, and_23_out);
  and and_23 (and_23_out, Function_Code[0], Function_Code[1], ~Function_Code[2], Function_Code[3], ~Function_Code[4], Function_Code[5], in_3);  // AND_Gate
  and and_24 (\nor , Neccesary_Condition, and_25_out);
  and and_25 (and_25_out, Function_Code[0], Function_Code[1], Function_Code[2], ~Function_Code[3], ~Function_Code[4], Function_Code[5], in_3);  // AND_Gate
  and and_26 (and_26_out, ~Operation_Code[0], ~Operation_Code[1], ~Operation_Code[2], Operation_Code[3], Operation_Code[4], Operation_Code[5], in_3);  // AND_Gate
  and and_27 (and_27_out, ~Function_Code[0], ~Function_Code[1], ~Function_Code[2], ~Function_Code[3], ~Function_Code[4], ~Function_Code[5], in_3);  // AND_Gate
  and and_28 (mflo, Neccesary_Condition, and_29_out);
  and and_29 (and_29_out, ~Function_Code[0], Function_Code[1], ~Function_Code[2], ~Function_Code[3], Function_Code[4], ~Function_Code[5], in_3);  // AND_Gate
  and and_30 (rnd, ONC, and_31_out);
  and and_31 (and_31_out, ~Function_Code[0], Function_Code[1], ~Function_Code[2], ~Function_Code[3], ~Function_Code[4], ~Function_Code[5], in_3);  // AND_Gate
  and and_32 (nop, Neccesary_Condition, and_17_out);
  and and_33 (pop, and_26_out, and_27_out);
  and and_34 (mult, Neccesary_Condition, and_35_out);
  and and_35 (and_35_out, ~Function_Code[0], ~Function_Code[1], ~Function_Code[2], Function_Code[3], Function_Code[4], ~Function_Code[5], in_3);  // AND_Gate
  and and_36 (divu, Neccesary_Condition, and_37_out);
  and and_37 (and_37_out, Function_Code[0], Function_Code[1], ~Function_Code[2], Function_Code[3], Function_Code[4], ~Function_Code[5], in_3);  // AND_Gate
  and and_38 (\and , Neccesary_Condition, and_39_out);
  and and_39 (and_39_out, ~Function_Code[0], ~Function_Code[1], Function_Code[2], ~Function_Code[3], ~Function_Code[4], Function_Code[5], in_3);  // AND_Gate
  and and_40 (\xor , Neccesary_Condition, and_41_out);
  and and_41 (and_41_out, ~Function_Code[0], ~Function_Code[1], ~Function_Code[2], Function_Code[3], ~Function_Code[4], Function_Code[5], in_3);  // AND_Gate
  and and_42 (jr, Neccesary_Condition, and_43_out);
  and and_43 (and_43_out, ~Function_Code[0], ~Function_Code[1], ~Function_Code[2], Function_Code[3], ~Function_Code[4], ~Function_Code[5], in_3);  // AND_Gate
  and and_44 (ONC, Operation_Code[0], Operation_Code[1], Operation_Code[2], Operation_Code[3], Operation_Code[4], Operation_Code[5], in_3);
  and and_45 (and_45_out, Function_Code[0], ~Function_Code[1], ~Function_Code[2], ~Function_Code[3], ~Function_Code[4], ~Function_Code[5], in_3);  // AND_Gate
  and and_46 (kbd, ONC, and_47_out);
  and and_47 (and_47_out, ~Function_Code[0], ~Function_Code[1], Function_Code[2], ~Function_Code[3], ~Function_Code[4], ~Function_Code[5], in_3);  // AND_Gate
  and and_48 (tty, ONC, and_45_out);

  // Other names for the same wires on the sheet: EN = in_3
endmodule

module ID_Op_Code_I (
  input  [5:0] Function_Code,
  input  in_2,
  output bltz,
  output addi,
  output stli,
  output stliu,
  output andi,
  output ori,
  output xori,
  output lw,
  output sw,
  output beq,
  output bne,
  output blez,
  output bgtz
);

  and and_1 (addi, ~Function_Code[0], ~Function_Code[1], ~Function_Code[2], Function_Code[3], ~Function_Code[4], ~Function_Code[5], in_2);  // AND_Gate
  and and_2 (andi, ~Function_Code[0], ~Function_Code[1], Function_Code[2], Function_Code[3], ~Function_Code[4], ~Function_Code[5], in_2);  // AND_Gate
  and and_3 (lw, Function_Code[0], Function_Code[1], ~Function_Code[2], ~Function_Code[3], ~Function_Code[4], Function_Code[5], in_2);  // AND_Gate
  and and_4 (bne, Function_Code[0], ~Function_Code[1], Function_Code[2], ~Function_Code[3], ~Function_Code[4], ~Function_Code[5], in_2);  // AND_Gate
  and and_5 (bltz, Function_Code[0], ~Function_Code[1], ~Function_Code[2], ~Function_Code[3], ~Function_Code[4], ~Function_Code[5], in_2);  // AND_Gate
  and and_6 (stli, ~Function_Code[0], Function_Code[1], ~Function_Code[2], Function_Code[3], ~Function_Code[4], ~Function_Code[5], in_2);  // AND_Gate
  and and_7 (ori, Function_Code[0], ~Function_Code[1], Function_Code[2], Function_Code[3], ~Function_Code[4], ~Function_Code[5], in_2);  // AND_Gate
  and and_8 (sw, Function_Code[0], Function_Code[1], ~Function_Code[2], Function_Code[3], ~Function_Code[4], Function_Code[5], in_2);  // AND_Gate
  and and_9 (blez, ~Function_Code[0], Function_Code[1], Function_Code[2], ~Function_Code[3], ~Function_Code[4], ~Function_Code[5], in_2);  // AND_Gate
  and and_10 (stliu, Function_Code[0], Function_Code[1], ~Function_Code[2], Function_Code[3], ~Function_Code[4], ~Function_Code[5], in_2);  // AND_Gate
  and and_11 (xori, ~Function_Code[0], Function_Code[1], Function_Code[2], Function_Code[3], ~Function_Code[4], ~Function_Code[5], in_2);  // AND_Gate
  and and_12 (beq, ~Function_Code[0], ~Function_Code[1], Function_Code[2], ~Function_Code[3], ~Function_Code[4], ~Function_Code[5], in_2);  // AND_Gate
  and and_13 (bgtz, Function_Code[0], Function_Code[1], Function_Code[2], ~Function_Code[3], ~Function_Code[4], ~Function_Code[5], in_2);  // AND_Gate

  // Other names for the same wires on the sheet: EN = in_2; Operation_Code[5:0] = Function_Code
endmodule

module ID_Op_Code_J (
  input  [5:0] Operation_Code,
  input  in_2,
  output jump
);

  and and_1 (jump, ~Operation_Code[0], Operation_Code[1], ~Operation_Code[2], ~Operation_Code[3], ~Operation_Code[4], ~Operation_Code[5], in_2);  // AND_Gate

  // Other names for the same wires on the sheet: EN = in_2
endmodule

module Control_Unit (
  input  in_1,
  input  in_2,
  input  in_3,
  input  in_4,
  input  in_5,
  input  in_6,
  input  in_7,
  input  in_8,
  input  in_9,
  input  in_10,
  input  in_11,
  input  in_12,
  output out_13,
  output out_14,
  output out_15,
  output out_16,
  output out_17,
  output out_18,
  output out_19,
  output out_20,
  output out_21
);

  wire branch, d_ff_1_q, d_ff_2_q, d_ff_3_q, d_ff_5_q, demultiplexer_1_out0, demultiplexer_1_out1, or_5_out,
       RF;
  wire [2:0] or_1_out;

  D_Flip_Flop #(.trigger("falling")) d_ff_1 (.clk(in_11), .D(in_4), .Q(d_ff_1_q));  // open: Qn, preset, en, reset
  or or_1 (or_1_out[0], in_7, in_6, in_2);
  or or_2 (or_1_out[1], in_7, in_9);
  or or_3 (or_1_out[2], in_10, in_2);
  D_Flip_Flop #(.trigger("falling")) d_ff_2 (
    .clk(in_11), .D(in_1), .Q(d_ff_2_q), .reset(in_12));  // open: Qn, preset, en
  Demultiplexer #(.select(3)) demultiplexer_1 (
    .out0(demultiplexer_1_out0), .out1(demultiplexer_1_out1), .out2(branch), .out3(RF), .out4(out_14),
    .out5(out_19), .in(d_ff_1_q), .sel(or_1_out));  // open: out6, out7, en
  or or_4 (out_16, d_ff_2_q, d_ff_3_q);
  D_Flip_Flop #(.trigger("falling")) d_ff_3 (
    .clk(in_11), .D(out_15), .Q(d_ff_3_q), .reset(in_12));  // open: Qn, preset, en
  or or_5 (or_5_out, out_21, demultiplexer_1_out0);
  D_Flip_Flop #(.trigger("falling")) d_ff_4 (
    .clk(in_11), .D(or_5_out), .Q(out_21), .reset(in_12));  // open: Qn, preset, en
  and and_1 (out_18, out_20, in_8);
  D_Flip_Flop #(.trigger("falling")) d_ff_5 (
    .clk(in_11), .D(demultiplexer_1_out1), .Q(d_ff_5_q), .reset(in_12));  // open: Qn, preset, en
  or or_6 (out_13, d_ff_5_q, RF, in_5);
  D_Flip_Flop #(.trigger("falling")) d_ff_6 (.clk(in_11), .D(out_13), .Q(out_20));  // open: Qn, preset, en, reset
  or or_7 (out_15, branch, in_3, out_20);

  assign out_17 = in_4;

  // Other names for the same wires on the sheet: alu_Inst = in_6; CLK = in_11; end = out_21; Get_Data = out_14;
  //   Get_Inst = out_16; jmp_Inst = in_9; mem_Inst = in_10; R_Inst = in_7; Ready_Data = in_5; Ready_Write = in_3;
  //   RST = in_12; Start = in_1; kbd_en = out_20; tty = out_20; tty_en = out_18; tty_Inst = in_8; Ready_Inst = in_4;
  //   use_Gl = in_4; Counter = out_15; use_PC = out_15; use_RF = out_13; Write = out_19; Write_Inst = in_2
endmodule

module Data_Path (
  input  in_1,
  input  in_2,
  input  in_3,
  input  in_4,
  input  in_5,
  input  in_6,
  input  in_7,
  input  in_8,
  input  [6:0] in_9,
  input  [31:0] in_10,
  output [6:0] out_11,
  output out_12,
  output out_13,
  output out_14,
  output out_15,
  output [31:0] out_16,
  output out_17,
  output out_18,
  output out_19,
  output out_20,
  output [31:0] out_21
);

  wire add, addi, \and , andi, beq, bgtz, blez, bltz, bne, div, divu, immediate, jr, jump, kbd, lw, mfhi,
       mflo, mult, mulu, N, nop, \nor , \or , or_3_out, ori, pop, push, rnd, sign, slt, slti, sltiu, sltu,
       sub, sw, \xor , xori, Z;
  wire [2:0] or_8_out;
  wire [3:0] ALU_OP;
  wire [4:0] multiplexer_3_out, Rd, Rs, Rt;
  wire [5:0] FuncCode, OpCode;
  wire [15:0] Constant;
  wire [25:0] Jump_Dest;
  wire [31:0] auxiliar_swapoutram_1_out_2, DATA_IN, Hi, Lo, multiplexer_2_out, PC_in, PC_out, R_ALU,
       random_1_out, register_1_q, Rt_t, SP;
  wire [31:7] Rs_t;
  wire [31:31] and_1_out;

  // Probe on auxiliar_swapoutram_1_out_2
  Auxiliar_SwapOutRam auxiliar_swapoutram_1 (.in_1(in_10), .out_2(auxiliar_swapoutram_1_out_2));
  or or_1 (out_13, \or , add, sub, mult, div, mulu, divu, addi, \and , \nor , \xor , andi, ori, xori, slt, slti, sltu, sltiu);
  Register #(.width(32)) register_1 (
    .D(auxiliar_swapoutram_1_out_2), .en(in_7), .Q(register_1_q), .clk(in_1), .clr(in_4));
  or or_2 (out_14, kbd, out_17, rnd, mfhi, mflo);
  Multiplexer #(.width(32)) multiplexer_1 (.in0({Rs_t, out_11}), .in1(Rt_t), .out(out_21), .sel(sw));  // open: en
  or or_3 (or_3_out, sw, addi, lw);
  ID_Intruction_Decoder id_intruction_decoder_1 (
    .Instruction(register_1_q), .out_10(nop), .out_12(addi), .out_14(add), .out_16(slti), .out_18(sub),
    .out_20(sltiu), .out_22(mult), .out_24(lw), .out_27(div), .out_29(beq), .out_31(\and ), .out_33(pop),
    .out_11(mulu), .out_13(andi), .out_15(divu), .out_17(ori), .out_19(slt), .out_21(xori), .out_23(sltu),
    .out_25(sw), .out_28(\or ), .out_30(bne), .out_32(\nor ), .out_34(\xor ), .out_38(push), .out_39(jr),
    .out_40(mfhi), .out_41(mflo), .out_42(out_12), .out_43(out_17), .out_44(rnd), .out_45(kbd),
    .out_35(bltz), .out_36(blez), .out_37(bgtz), .out_26(jump), .out_4(FuncCode), .out_3(OpCode), .out_5(Rd),
    .out_6(Rt), .out_7(Rs), .out_8(Constant), .out_9(Jump_Dest), .in_2(in_8));
  ALU_Encoder alu_encoder_1 (
    .in_1(add), .in_3(sub), .in_4(mult), .in_5(mulu), .in_2(or_3_out), .in_9(sltu), .in_10(slti),
    .in_12(\and ), .in_14(\or ), .in_16(\nor ), .in_17(\xor ), .Code_Operation(ALU_OP), .in_6(div),
    .in_7(divu), .in_8(slt), .in_11(sltiu), .in_13(andi), .in_15(ori), .in_18(xori), .Immediate(immediate),
    .sign(sign));
  or or_4 (out_20, push, sw);
  or or_5 (out_19, push, pop);
  or or_6 (out_18, lw, sw);
  or or_7 (out_15, bgtz, bne, beq, blez, bltz, jr, jump, nop);
  and and_1 (and_1_out[31], ~xori, ~andi, ~ori, Constant[15]);  // AND_Gate
  Auxiliar_GetMemoryAddress auxiliar_getmemoryaddress_1 (
    .in_1(PC_out), .in_2(R_ALU), .in_3(SP), .in_4(lw), .in_5(sw), .in_6(pop), .in_7(push), .in_8(in_6),
    .OUTPUT(out_16));
  Branch_Control branch_control_1 (
    .in_1(beq), .in_2(bne), .in_3(bltz), .in_4(jr), .in_5(blez), .in_6(bgtz), .in_7(jump), .in_8(Jump_Dest),
    .in_9({Rs_t, out_11}), .in_10(Rt_t), .in_11(PC_out), .in_12(Constant), .OUTPUT(PC_in));
  Multiplexer #(.width(32)) multiplexer_2 (
    .in0(Rt_t), .in1({{16{and_1_out[31]}}, Constant}), .out(multiplexer_2_out), .sel(immediate));  // open: en
  Multiplexer #(.width(5)) multiplexer_3 (.in0(Rd), .in1(Rt), .out(multiplexer_3_out), .sel(immediate));  // open: en
  Random #(.width(32)) random_1 (.clk(in_1), .next(rnd), .out(random_1_out));  // open: clr
  or or_8 (or_8_out[0], lw, pop, mflo, kbd);
  or or_9 (or_8_out[1], mfhi, mflo);
  or or_10 (or_8_out[2], rnd, kbd);
  ALU alu_1 (
    .A({Rs_t, out_11}), .B(multiplexer_2_out), .Operation(ALU_OP), .Z(Z), .N(N), .RESULT_OPERATION(R_ALU),
    .in_4(sign), .in_5(in_1), .Lo_2(Lo), .Lo(Hi));
  PC pc_1 (.IPC(PC_in), .OPC(PC_out), .ENABLE(in_5), .RESET(in_4), .CLOCK(in_1));
  Multiplexer #(.select(3), .width(32)) multiplexer_4 (
    .in0(R_ALU), .in1(in_10), .in2(Hi), .in3(Lo), .in4(random_1_out), .in5({{25{1'b0}}, in_9}),
    .out(DATA_IN), .sel(or_8_out));  // open: in6, in7, en
  Register_File register_file_1 (
    .in_1(DATA_IN), .AA(Rs), .BA(Rt), .DA(multiplexer_3_out), .RESET(in_4), .READ_WRITE(in_2),
    .A({Rs_t, out_11}), .B(Rt_t), .CLOCK(in_1), .PUSH(push), .POP(pop), .IN_PC(in_5), .SP(SP));

  // Other names for the same wires on the sheet: kbd_Data[6:0] = in_9; ADDRESS[31:0] = out_16; ALU_Inst = out_13;
  //   CLK = in_1; EN = in_8; EN_GI = in_7; EN_PC = in_5; EN_RF = in_2; half = out_12; INSTRUCTION[31:0] = in_10;
  //   Jump_Inst = out_15; kbd_Ava = in_3; Memo_Inst = out_18; Next_Inst = in_6; R_Inst = out_14;
  //   R_Output[31:0] = out_21; Rs_t[6:0] = out_11; tty_Data[6:0] = out_11; RST = in_4; Stack_Inst = out_19;
  //   tty = out_17; Write_Inst = out_20
endmodule

module Memory_Read (
  input  in_1,
  input  in_2,
  input  in_3,
  input  [3:0] in_4,
  input  [31:0] in_5,
  input  [31:0] in_6,
  input  [31:0] in_7,
  input  [31:0] in_8,
  output out_9,
  output CS,
  output [31:0] out_11,
  output [31:0] out_12,
  output [31:0] out_13,
  output [31:0] out_14
);

  wire enX, enY, or_1_out, STOP;

  or or_1 (or_1_out, in_1, STOP);
  D_Flip_Flop #(.trigger("falling")) d_ff_1 (.clk(in_2), .D(in_1), .Q(enY), .en(or_1_out));  // open: Qn, preset, reset
  Register #(.width(32)) register_1 (.D(in_5), .en(enX), .Q(out_11), .clk(in_2), .clr(in_3));
  Register #(.width(32)) register_2 (.D(in_7), .en(enX), .Q(out_13), .clk(in_2), .clr(in_3));
  Auxiliar_Counter auxiliar_counter_1 (.in_1(enY), .in_2(out_9), .in_3(in_2), .in_4(in_4), .READY(STOP));
  D_Flip_Flop #(.trigger("falling")) d_ff_2 (.clk(in_2), .D(STOP), .Q(enX), .reset(out_9));  // open: Qn, preset, en
  Register #(.width(32)) register_3 (.D(in_6), .en(enX), .Q(out_12), .clk(in_2), .clr(in_3));
  Register #(.width(32)) register_4 (.D(in_8), .en(enX), .Q(out_14), .clk(in_2), .clr(in_3));
  D_Flip_Flop #(.trigger("falling")) d_ff_3 (.clk(in_2), .D(enX), .Q(out_9));  // open: Qn, preset, en, reset
  or or_2 (CS, enX, enY);

  // Other names for the same wires on the sheet: CLK = in_2; GET = in_1; IN_Bank0[31:0] = in_5; IN_Bank1[31:0] = in_6;
  //   IN_Bank2[31:0] = in_7; IN_Bank3[31:0] = in_8; Out_Bank0[31:0] = out_11; Out_Bank1[31:0] = out_12;
  //   Out_Bank2[31:0] = out_13; Out_Bank3[31:0] = out_14; READY = out_9; RST = in_3; TIME[3:0] = in_4
endmodule

module RAM_Handler (
  input  in_1,
  input  in_2,
  input  [31:0] in_3,
  input  [31:0] in_4,
  input  [31:0] in_5,
  input  [31:0] in_6,
  input  [3:0] in_7,
  input  in_8,
  input  [3:0] in_9,
  input  in_10,
  input  in_11,
  input  in_12,
  input  [31:0] in_13,
  output [3:0] out_14,
  output [15:0] out_15,
  output [31:0] out_16,
  output [31:0] out_17,
  output [31:0] out_18,
  output [31:0] out_19,
  output out_20,
  output out_21,
  output out_22,
  output out_23,
  output out_24
);

  wire CSData, CSInst, or_1_out, stop;
  wire [31:0] auxiliar_swapoutram_1_out_2, auxiliar_swapoutram_2_out_2, auxiliar_swapoutram_3_out_2,
       auxiliar_swapoutram_4_out_2, DO0, DO1, DO2, DO3, IO0, IO1, IO2, IO3;

  or or_1 (or_1_out, in_8, stop);
  D_Flip_Flop #(.trigger("falling")) d_ff_1 (
    .clk(in_1), .D(in_8), .Q(out_20), .en(or_1_out));  // open: Qn, preset, reset
  Memory_Read memory_read_1 (
    .in_1(in_11), .in_2(in_1), .in_3(in_2), .in_4(in_7), .in_5(in_3), .in_6(in_4), .in_7(in_5), .in_8(in_6),
    .out_9(out_21), .CS(CSInst), .out_11(IO0), .out_12(IO1), .out_13(IO2), .out_14(IO3));
  Auxiliar_Counter auxiliar_counter_1 (.in_1(out_20), .in_2(out_24), .in_3(in_1), .in_4(in_9), .READY(stop));
  D_Flip_Flop #(.trigger("falling")) d_ff_2 (.clk(in_1), .D(stop), .Q(out_24));  // open: Qn, preset, en, reset
  Memory_Read memory_read_2 (
    .in_1(in_10), .in_2(in_1), .in_3(in_2), .in_4(in_7), .in_5(in_3), .in_6(in_4), .in_7(in_5), .in_8(in_6),
    .out_9(out_22), .CS(CSData), .out_11(DO0), .out_12(DO1), .out_13(DO2), .out_14(DO3));
  or or_2 (out_23, CSData, out_20, CSInst);
  Auxiliar_SwapOutRam auxiliar_swapoutram_1 (.in_1(DO0), .out_2(auxiliar_swapoutram_1_out_2));
  Auxiliar_SwapOutRam auxiliar_swapoutram_2 (.in_1(DO1), .out_2(auxiliar_swapoutram_2_out_2));
  Auxiliar_SwapOutRam auxiliar_swapoutram_3 (.in_1(DO2), .out_2(auxiliar_swapoutram_3_out_2));
  Auxiliar_SwapOutRam auxiliar_swapoutram_4 (.in_1(DO3), .out_2(auxiliar_swapoutram_4_out_2));
  Demultiplexer #(.select(2)) demultiplexer_1 (
    .out0(out_14[0]), .out1(out_14[1]), .out2(out_14[2]), .out3(out_14[3]), .in(1'b1), .sel(in_13[3:2]));  // open: en
  Multiplexer #(.width(32)) multiplexer_1 (
    .in0(auxiliar_swapoutram_1_out_2), .in1(IO0), .out(out_16), .sel(in_12));  // open: en
  Multiplexer #(.width(32)) multiplexer_2 (
    .in0(auxiliar_swapoutram_2_out_2), .in1(IO1), .out(out_17), .sel(in_12));  // open: en
  Multiplexer #(.width(32)) multiplexer_3 (
    .in0(auxiliar_swapoutram_3_out_2), .in1(IO2), .out(out_18), .sel(in_12));  // open: en
  Multiplexer #(.width(32)) multiplexer_4 (
    .in0(auxiliar_swapoutram_4_out_2), .in1(IO3), .out(out_19), .sel(in_12));  // open: en

  assign out_15 = in_13[19:4];

  // Other names for the same wires on the sheet: CLK = in_1; CS = out_23; DP_Address[31:0] = in_13;
  //   ADDR[15:0] = in_13[19:4]; get_Data = in_10; get_Inst = in_11; IN_Bank0[31:0] = in_3; IN_Bank1[31:0] = in_4;
  //   IN_Bank2[31:0] = in_5; IN_Bank3[31:0] = in_6; Is_An_Inst = in_12; MASK[3:0] = out_14; Out_Bank0[31:0] = out_16;
  //   Out_Bank1[31:0] = out_17; Out_Bank2[31:0] = out_18; Out_Bank3[31:0] = out_19; R_W = out_20;
  //   Read_Time[3:0] = in_7; Ready_Data = out_22; Ready_Inst = out_21; Ready_Write = out_24; RST = in_2; Write = in_8;
  //   Write_Time[3:0] = in_9
endmodule

module Auxiliar_SwapOutRam (
  input  [31:0] in_1,
  output [31:0] out_2
);


  assign out_2 = {in_1[7:0], in_1[15:8], in_1[23:16], in_1[31:24]};
endmodule

module Auxiliar_GetMemoryAddress (
  input  [31:0] in_1,
  input  [31:0] in_2,
  input  [31:0] in_3,
  input  in_4,
  input  in_5,
  input  in_6,
  input  in_7,
  input  in_8,
  output [31:0] OUTPUT
);

  wire [1:0] or_2_out;
  wire [31:0] multiplexer_1_out, subtractor_1_out;

  Subtractor #(.width(32)) subtractor_1 (.a(in_3), .b(32'h4), .out(subtractor_1_out));  // open: bin, bout
  Multiplexer #(.width(32)) multiplexer_1 (
    .in0(in_3), .in1(subtractor_1_out), .out(multiplexer_1_out), .sel(in_7));  // open: en
  or or_1 (or_2_out[1], in_6, in_8, in_7);
  Multiplexer #(.select(2), .width(32)) multiplexer_2 (
    .in0(in_1), .in1(in_2), .in2(multiplexer_1_out), .in3(in_1), .out(OUTPUT), .sel(or_2_out));  // open: en
  or or_2 (or_2_out[0], in_4, in_8, in_5);

  // Other names for the same wires on the sheet: Is_a_PC = in_8; lw = in_4; PC[31:0] = in_1; pop = in_6; push = in_7;
  //   R_ALU[31:0] = in_2; SP[31:0] = in_3; sw = in_5
endmodule

module Auxiliar_Counter (
  input  in_1,
  input  in_2,
  input  in_3,
  input  [3:0] in_4,
  output READY
);

  wire [3:0] counter_1_q;

  Counter #(.width(4), .max('hf)) counter_1 (
    .count(in_1), .Q(counter_1_q), .clk(in_3), .clr(in_2));  // open: load, D, carry
  Comparator #(.width(4)) comparator_1 (.a(in_4), .b(counter_1_q), .eq(READY));  // open: gt, lt

  // Other names for the same wires on the sheet: CLOCK = in_3; RESET = in_2; START = in_1; TIME[3:0] = in_4
endmodule
